// Digital circuit DRAM.dig as structural Verilog
module DRAM (
  input  Clock,
  input  [1:0] Control_Load_Store_Reset,
  input  [1:0] Memory_Control_IR__Load__Store__Reset,
  input  [1:0] Control_PC__Load__INC__Reset,
  input  [3:0] Input_Mem,
  input  PC_orindep,
  input  [3:0] Address,
  output [3:0] Output
);

  wire [3:0] _4_bit_programcounter_1_output, gpr_1_output, multiplexer_1_out;

  Multiplexer #(.Bits(4)) multiplexer_1 (
    .sel(PC_orindep), .in_0(_4_bit_programcounter_1_output), .in_1(Address), .out(multiplexer_1_out));
  GPR gpr_1 (
    .Control(Control_Load_Store_Reset), .Input(Input_Mem), .Clock(Clock), .Address(multiplexer_1_out),
    .Output(gpr_1_output));
  _4_bit_ProgramCounter _4_bit_programcounter_1 (
    .clk(Clock), .Control(Control_PC__Load__INC__Reset), .Output(_4_bit_programcounter_1_output));
  FourBitInstructionRegister fourbitinstructionregister_1 (
    .Clock(Clock), .Control(Memory_Control_IR__Load__Store__Reset), .Input(gpr_1_output), .Output(Output));
endmodule
