// Digital circuit GPR.dig as structural Verilog
module GPR (
  input  [1:0] Control,
  input  [3:0] Input,
  input  Clock,
  input  [3:0] Address,
  output [3:0] Output
);

  wire and_1_out, and_2_out, and_3_out, and_4_out, and_5_out, and_6_out, and_7_out, and_8_out, and_9_out,
       and_10_out, and_11_out, and_12_out, and_13_out, and_14_out, and_15_out, and_16_out, decoder_1_out_0,
       decoder_1_out_1, decoder_1_out_2, decoder_1_out_3, decoder_1_out_4, decoder_1_out_5, decoder_1_out_6,
       decoder_1_out_7, decoder_1_out_8, decoder_1_out_9, decoder_1_out_10, decoder_1_out_11,
       decoder_1_out_12, decoder_1_out_13, decoder_1_out_14, decoder_1_out_15;
  wire [3:0] fourbitregister_1_p4, fourbitregister_2_p4, fourbitregister_3_p4, fourbitregister_4_p4,
       fourbitregister_5_p4, fourbitregister_6_p4, fourbitregister_7_p4, fourbitregister_8_p4,
       fourbitregister_9_p4, fourbitregister_10_p4, fourbitregister_11_p4, fourbitregister_12_p4,
       fourbitregister_13_p4, fourbitregister_14_p4, fourbitregister_15_p4, fourbitregister_16_p4;

  Decoder #(.Selector_Bits(4)) decoder_1 (
    .sel(Address), .out_0(decoder_1_out_0), .out_1(decoder_1_out_1), .out_2(decoder_1_out_2),
    .out_3(decoder_1_out_3), .out_4(decoder_1_out_4), .out_5(decoder_1_out_5), .out_6(decoder_1_out_6),
    .out_7(decoder_1_out_7), .out_8(decoder_1_out_8), .out_9(decoder_1_out_9), .out_10(decoder_1_out_10),
    .out_11(decoder_1_out_11), .out_12(decoder_1_out_12), .out_13(decoder_1_out_13),
    .out_14(decoder_1_out_14), .out_15(decoder_1_out_15));
  and and_1 (and_1_out, Clock, decoder_1_out_0);
  and and_2 (and_2_out, Clock, decoder_1_out_1);
  and and_3 (and_3_out, Clock, decoder_1_out_2);
  and and_4 (and_4_out, Clock, decoder_1_out_3);
  and and_5 (and_5_out, Clock, decoder_1_out_4);
  and and_6 (and_6_out, Clock, decoder_1_out_5);
  and and_7 (and_7_out, Clock, decoder_1_out_6);
  and and_8 (and_8_out, Clock, decoder_1_out_7);
  and and_9 (and_9_out, Clock, decoder_1_out_8);
  and and_10 (and_10_out, Clock, decoder_1_out_9);
  and and_11 (and_11_out, Clock, decoder_1_out_10);
  and and_12 (and_12_out, Clock, decoder_1_out_11);
  and and_13 (and_13_out, Clock, decoder_1_out_12);
  and and_14 (and_14_out, Clock, decoder_1_out_13);
  and and_15 (and_15_out, Clock, decoder_1_out_14);
  and and_16 (and_16_out, Clock, decoder_1_out_15);
  // FourBitRegister fourbitregister_1: pin names not known; wires that end beside it: and_1_out, Control, Input, fourbitregister_1_p4
  // FourBitRegister fourbitregister_2: pin names not known; wires that end beside it: and_2_out, Control, Input, fourbitregister_2_p4
  // FourBitRegister fourbitregister_3: pin names not known; wires that end beside it: and_3_out, Control, Input, fourbitregister_3_p4
  // FourBitRegister fourbitregister_4: pin names not known; wires that end beside it: and_4_out, Control, Input, fourbitregister_4_p4
  // FourBitRegister fourbitregister_5: pin names not known; wires that end beside it: and_5_out, Control, Input, fourbitregister_5_p4
  // FourBitRegister fourbitregister_6: pin names not known; wires that end beside it: and_6_out, Control, Input, fourbitregister_6_p4
  // FourBitRegister fourbitregister_7: pin names not known; wires that end beside it: and_7_out, Control, Input, fourbitregister_7_p4
  // FourBitRegister fourbitregister_8: pin names not known; wires that end beside it: and_8_out, Control, Input, fourbitregister_8_p4
  // FourBitRegister fourbitregister_9: pin names not known; wires that end beside it: and_9_out, Control, Input, fourbitregister_9_p4
  // FourBitRegister fourbitregister_10: pin names not known; wires that end beside it: and_10_out, Control, Input, fourbitregister_10_p4
  // FourBitRegister fourbitregister_11: pin names not known; wires that end beside it: and_11_out, Control, Input, fourbitregister_11_p4
  // FourBitRegister fourbitregister_12: pin names not known; wires that end beside it: and_12_out, Control, Input, fourbitregister_12_p4
  // FourBitRegister fourbitregister_13: pin names not known; wires that end beside it: and_13_out, Control, Input, fourbitregister_13_p4
  // FourBitRegister fourbitregister_14: pin names not known; wires that end beside it: and_14_out, Control, Input, fourbitregister_14_p4
  // FourBitRegister fourbitregister_15: pin names not known; wires that end beside it: and_15_out, Control, Input, fourbitregister_15_p4
  // FourBitRegister fourbitregister_16: pin names not known; wires that end beside it: and_16_out, Control, Input, fourbitregister_16_p4
  Multiplexer #(.Selector_Bits(4), .Bits(4)) multiplexer_1 (
    .sel(Address), .in_0(fourbitregister_1_p4), .in_1(fourbitregister_2_p4), .in_2(fourbitregister_3_p4),
    .in_3(fourbitregister_4_p4), .in_4(fourbitregister_5_p4), .in_5(fourbitregister_6_p4),
    .in_6(fourbitregister_7_p4), .in_7(fourbitregister_8_p4), .in_8(fourbitregister_9_p4),
    .in_9(fourbitregister_10_p4), .in_10(fourbitregister_11_p4), .in_11(fourbitregister_12_p4),
    .in_12(fourbitregister_13_p4), .in_13(fourbitregister_14_p4), .in_14(fourbitregister_15_p4),
    .in_15(fourbitregister_16_p4), .out(Output));
endmodule
